# Fritzing sketch clock (saved by Fritzing 0.5.2b)
breadboards: 2

parts:
  IC1 = IC, DIP package, 20 pins [chip_label=PIC16F690 spacing=300mil]
  IC2 = IC, DIP package, 16 pins [chip_label=DS1305 spacing=300mil]
  R1 = Resistor [resistance=220 package=THT]
  XTAL1 = Crystal [package=THT]
  J1 = female pin header, 6 pins [form="♂ (male)"]
  C1 = Ceramic Capacitor [package=THT]
  R2 = Resistor [resistance=220 package=THT]
  Power_plug1 = Power plug
  C2 = Ceramic Capacitor [package=THT]
  C3 = Ceramic Capacitor [package=THT]
  IC3 = IC, DIP package, 24 pins [chip_label=MAX7219 spacing=300mil]
  IC4 = IC, DIP package, 18 pins [chip_label="2digit 7seg" spacing=600mil]
  IC5 = IC, DIP package, 18 pins [chip_label="2digit 7seg" spacing=600mil]
  IC6 = IC, DIP package, 18 pins [chip_label="2digit 7seg" spacing=600mil]
  S1 = Pushbutton [package="[THT]"]
  S2 = Pushbutton [package="[THT]"]
  S3 = Pushbutton [package="[THT]"]

nets:
  N1: IC1.pin1, J1.pin2, C1.pin_0, Power_plug1.VCC
  N2: IC1.pin2, S2.Pin_1, S2.Pin_2
  N3: IC1.pin3, S3.Pin_1, S3.Pin_2
  N4: IC1.pin4, J1.pin1
  N5: IC1.pin9, IC2.pin12, IC3.pin1
  N6: IC1.pin10, IC2.pin10
  N7: IC1.pin11, IC2.pin11, IC3.pin13
  N8: IC1.pin12, IC3.pin12
  N9: IC1.pin13, IC2.pin13
  N10: IC1.pin17, S1.Pin_1, S1.Pin_2
  N11: IC1.pin18, J1.pin5
  N12: IC1.pin19, J1.pin4
  N13: IC1.pin20, J1.pin3, C1.pin_1, Power_plug1.GND, S1.Pin_3, S1.Pin_4, S2.Pin_3, S2.Pin_4, S3.Pin_3, S3.Pin_4
  N14: IC2.pin1, IC2.pin8, R1.Pin_1, C2.pin_0, C3.pin_0, IC3.pin4, IC3.pin9
  N15: IC2.pin2, R1.Pin_0
  N16: IC2.pin3, XTAL1.pin_0
  N17: IC2.pin4, XTAL1.pin_1
  N18: IC2.pin9, IC2.pin14, IC2.pin16, R2.Pin_0, C2.pin_1, C3.pin_1, IC3.pin19
  N19: R2.Pin_1, IC3.pin18
  N20: IC3.pin2, IC4.pin14
  N21: IC3.pin3, IC6.pin14
  N22: IC3.pin6, IC5.pin14
  N23: IC3.pin7, IC5.pin13
  N24: IC3.pin10, IC6.pin13
  N25: IC3.pin11, IC4.pin13
  N26: IC3.pin14, IC4.pin11, IC4.pin16, IC5.pin11, IC5.pin16, IC6.pin11, IC6.pin16
  N27: IC3.pin15, IC4.pin12, IC4.pin18, IC5.pin12, IC5.pin18, IC6.pin12, IC6.pin18
  N28: IC3.pin16, IC4.pin10, IC4.pin15, IC5.pin10, IC5.pin15, IC6.pin10, IC6.pin15
  N29: IC3.pin17, IC4.pin7, IC4.pin17, IC5.pin7, IC5.pin17, IC6.pin7, IC6.pin17
  N30: IC3.pin20, IC4.pin3, IC4.pin8, IC5.pin3, IC5.pin8, IC6.pin3, IC6.pin8
  N31: IC3.pin21, IC4.pin1, IC4.pin5, IC5.pin1, IC5.pin5, IC6.pin1, IC6.pin5
  N32: IC3.pin22, IC4.pin4, IC4.pin9, IC5.pin4, IC5.pin9, IC6.pin4, IC6.pin9
  N33: IC3.pin23, IC4.pin2, IC4.pin6, IC5.pin2, IC5.pin6, IC6.pin2, IC6.pin6

notes:
  Red = +5V
  Black = GND
  Yellow = +12V (PICkit2)
  Green = ICSP
  Brown = SPI Bus
  Purple = Common Cathode
  Blue = Anodes
  Grey = Buttons
